// Logisim project VoteCounter.circ as structural Verilog: 5 circuits, main circuit main
module main (
  input  YES,
  input  NO,
  input  YES_2,
  input  NO_2,
  input  YES_3,
  input  NO_3,
  input  YES_4,
  input  NO_4,
  input  YES_5,
  input  NO_5,
  input  YES_6,
  input  NO_6
);

  wire a1, a2, b1, b2, c1, c2, d1, d2, e1, e2, f1, f2, g1, g2;

  Vote_Counter vote_counter_1 (
    .YES(YES), .NO(NO), .YES_2(YES_2), .NO_2(NO_2), .YES_3(YES_3), .NO_3(NO_3), .YES_4(YES_4), .NO_4(NO_4),
    .YES_5(YES_5), .NO_5(NO_5), .YES_6(YES_6), .NO_6(NO_6), .a1(a1), .b1(b1), .c1(c1), .d1(d1), .e1(e1),
    .f1(f1), .g1(g1), .a2(a2), .b2(b2), .c2(c2), .d2(d2), .e2(e2), .f2(f2), .g2(g2));
  _7_Segment_Display u_7_segment_display_1 (.g(g1), .f(f1), .a(a1), .b(b1), .e(e1), .d(d1), .c(c1));  // open: dp
  _7_Segment_Display u_7_segment_display_2 (.g(g2), .f(f2), .a(a2), .b(b2), .e(e2), .d(d2), .c(c2));  // open: dp

  // Notes on the sheet:
  //   YES VOTES 
  //   NO VOTES
endmodule

module Switch (
  input  in_1,
  input  in_2,
  output out_3,
  output out_4
);

  Demultiplexer #(.select(2), .enable("false")) demultiplexer_1 (
    .out1(out_3), .out2(out_4), .in(1'b1), .sel({in_2, in_1}));  // open: out0, out3
endmodule

module Paralel_Adder (
  input  Cin,
  input  A0,
  input  B0,
  input  A1,
  input  B1,
  input  C0,
  input  C1,
  input  D0,
  input  D1,
  output Sum_0,
  output Sum_1,
  output Sum_2,
  output Sum_3,
  output Cout
);

  wire adder_1_cout, adder_2_cout, adder_3_cout;

  Adder #(.width(1)) adder_1 (.a(A0), .b(B0), .out(Sum_0), .cin(Cin), .cout(adder_1_cout));
  Adder #(.width(1)) adder_2 (.a(A1), .b(B1), .out(Sum_1), .cin(adder_1_cout), .cout(adder_2_cout));
  Adder #(.width(1)) adder_3 (.a(C0), .b(C1), .out(Sum_2), .cin(adder_2_cout), .cout(adder_3_cout));
  Adder #(.width(1)) adder_4 (.a(D0), .b(D1), .out(Sum_3), .cin(adder_3_cout), .cout(Cout));
endmodule

module BCD_to_7_Segment_Decoder (
  input  A,
  input  B,
  input  C,
  input  D,
  output a_2,
  output b_2,
  output c_2,
  output d_2,
  output e,
  output f,
  output g
);

  wire and_1_out, and_2_out, and_3_out, and_4_out, and_5_out, and_6_out, and_7_out, and_8_out, and_9_out,
       and_10_out, and_11_out, and_12_out, and_13_out, and_14_out, and_15_out, and_16_out, not_1_out,
       not_2_out, not_3_out, not_4_out, not_5_out, not_6_out, not_7_out, not_8_out, not_9_out, not_10_out,
       not_11_out, not_12_out, not_13_out, not_14_out, not_15_out, not_16_out, not_17_out, not_18_out,
       not_19_out, not_20_out, not_21_out, not_22_out;

  not not_1 (not_1_out, B);
  and and_1 (and_1_out, not_1_out, not_2_out);
  not not_2 (not_2_out, D);
  and and_2 (and_2_out, B, D);
  not not_3 (not_3_out, A);
  not not_4 (not_4_out, C);
  and and_3 (and_3_out, not_3_out, not_4_out, not_5_out);
  not not_5 (not_5_out, D);
  not not_6 (not_6_out, B);
  and and_4 (and_4_out, C, D);
  not not_7 (not_7_out, C);
  or or_1 (c_2, not_7_out, D, B);
  not not_8 (not_8_out, B);
  and and_5 (and_5_out, not_8_out, not_9_out);
  not not_9 (not_9_out, D);
  not not_10 (not_10_out, B);
  and and_6 (and_6_out, not_10_out, C);
  and and_7 (and_7_out, C, not_11_out);
  not not_11 (not_11_out, D);
  and and_8 (and_8_out, B, not_12_out, D);
  not not_12 (not_12_out, C);
  not not_13 (not_13_out, B);
  and and_9 (and_9_out, not_13_out, not_14_out);
  not not_14 (not_14_out, D);
  and and_10 (and_10_out, C, not_15_out);
  not not_15 (not_15_out, D);
  not not_16 (not_16_out, C);
  and and_11 (and_11_out, not_16_out, not_17_out);
  not not_17 (not_17_out, D);
  and and_12 (and_12_out, B, not_18_out);
  not not_18 (not_18_out, C);
  and and_13 (and_13_out, B, not_19_out);
  not not_19 (not_19_out, D);
  not not_20 (not_20_out, B);
  and and_14 (and_14_out, not_20_out, C);
  and and_15 (and_15_out, B, not_21_out);
  not not_21 (not_21_out, C);
  and and_16 (and_16_out, B, not_22_out);
  not not_22 (not_22_out, D);
  or or_2 (a_2, and_1_out, C, and_2_out, A);
  or or_3 (b_2, and_3_out, not_6_out, and_4_out);
  or or_4 (d_2, and_5_out, and_6_out, and_7_out, and_8_out, A);
  or or_5 (e, and_9_out, and_10_out);
  or or_6 (f, and_11_out, and_12_out, and_13_out, A);
  or or_7 (g, and_14_out, and_15_out, and_16_out, A);
endmodule

module Vote_Counter (
  input  YES,
  input  NO,
  input  YES_2,
  input  NO_2,
  input  YES_3,
  input  NO_3,
  input  YES_4,
  input  NO_4,
  input  YES_5,
  input  NO_5,
  input  YES_6,
  input  NO_6,
  output a1,
  output b1,
  output c1,
  output d1,
  output e1,
  output f1,
  output g1,
  output a2,
  output b2,
  output c2,
  output d2,
  output e2,
  output f2,
  output g2
);

  wire adder_1_cout, adder_1_out, adder_2_cout, adder_2_out, adder_3_cout, adder_3_out, adder_4_cout,
       adder_4_out, paralel_adder_1_sum_0, paralel_adder_1_sum_1, paralel_adder_1_sum_2,
       paralel_adder_2_sum_0, paralel_adder_2_sum_1, paralel_adder_2_sum_2, switch_1_out_3, switch_1_out_4,
       switch_2_out_3, switch_2_out_4, switch_3_out_3, switch_3_out_4, switch_4_out_3, switch_4_out_4,
       switch_5_out_3, switch_5_out_4, switch_6_out_3, switch_6_out_4;

  Switch switch_1 (.in_1(YES), .in_2(NO), .out_3(switch_1_out_3), .out_4(switch_1_out_4));
  Switch switch_2 (.in_1(YES_2), .in_2(NO_2), .out_3(switch_2_out_3), .out_4(switch_2_out_4));
  Switch switch_3 (.in_1(YES_3), .in_2(NO_3), .out_3(switch_3_out_3), .out_4(switch_3_out_4));
  Switch switch_4 (.in_1(YES_4), .in_2(NO_4), .out_3(switch_4_out_3), .out_4(switch_4_out_4));
  Switch switch_5 (.in_1(YES_5), .in_2(NO_5), .out_3(switch_5_out_3), .out_4(switch_5_out_4));
  Switch switch_6 (.in_1(YES_6), .in_2(NO_6), .out_3(switch_6_out_3), .out_4(switch_6_out_4));
  Adder #(.width(1)) adder_1 (
    .a(switch_1_out_3), .b(switch_2_out_3), .out(adder_1_out), .cin(switch_3_out_3), .cout(adder_1_cout));
  Adder #(.width(1)) adder_2 (
    .a(switch_4_out_3), .b(switch_5_out_3), .out(adder_2_out), .cin(switch_6_out_3), .cout(adder_2_cout));
  Adder #(.width(1)) adder_3 (
    .a(switch_1_out_4), .b(switch_2_out_4), .out(adder_3_out), .cin(switch_3_out_4), .cout(adder_3_cout));
  Adder #(.width(1)) adder_4 (
    .a(switch_4_out_4), .b(switch_5_out_4), .out(adder_4_out), .cin(switch_6_out_4), .cout(adder_4_cout));
  Paralel_Adder paralel_adder_1 (
    .A0(adder_1_out), .B0(adder_2_out), .A1(adder_1_cout), .B1(adder_2_cout), .C0(1'b0), .C1(1'b0),
    .D0(1'b0), .D1(1'b0), .Cin(1'b0), .Sum_0(paralel_adder_1_sum_0), .Sum_1(paralel_adder_1_sum_1),
    .Sum_2(paralel_adder_1_sum_2));  // open: Cout, Sum_3
  Paralel_Adder paralel_adder_2 (
    .A0(adder_3_out), .B0(adder_4_out), .A1(adder_3_cout), .B1(adder_4_cout), .C0(1'b0), .C1(1'b0),
    .D0(1'b0), .D1(1'b0), .Cin(1'b0), .Sum_0(paralel_adder_2_sum_0), .Sum_1(paralel_adder_2_sum_1),
    .Sum_2(paralel_adder_2_sum_2));  // open: Cout, Sum_3
  BCD_to_7_Segment_Decoder bcd_to_7_segment_decoder_1 (
    .A(1'b0), .B(paralel_adder_1_sum_2), .C(paralel_adder_1_sum_1), .D(paralel_adder_1_sum_0), .a_2(a1),
    .b_2(b1), .c_2(c1), .d_2(d1), .e(e1), .f(f1), .g(g1));
  BCD_to_7_Segment_Decoder bcd_to_7_segment_decoder_2 (
    .A(1'b0), .B(paralel_adder_2_sum_2), .C(paralel_adder_2_sum_1), .D(paralel_adder_2_sum_0), .a_2(a2),
    .b_2(b2), .c_2(c2), .d_2(d2), .e(e2), .f(f2), .g(g2));
endmodule
